# Fritzing sketch KY-015 (saved by Fritzing 0.9.3b)
circuit board: 8.46667cm x 5.64444cm
breadboards: 1

parts:
  Componente1 = Arduino Uno (Rev3) - ICSP
  Componente2 = Humidity Sensor - HIH-4030 Breakout

nets:
  N1: Componente1.D8, Componente2.OUT
  GND: Componente1.GND, Componente2.GND
  5V: Componente1.5V, Componente2.VCC
