# Fritzing sketch KY-016 (saved by Fritzing 0.9.3b)
breadboards: 1

parts:
  Componente1 = Arduino Nano (Rev3.0)
  Part1 = KY-016 RGB Full Color LED Module [package="Breakout board"]

nets:
  N1: Componente1.GND, Part1.-

custom parts:
  KY-016 RGB Full Color LED Module: KY-016 Arduino full color 5mm RGB LED, different colors can be obtained by mixing the three primary colors.
